# Fritzing sketch GPS-APRS Schematic (saved by Fritzing 0.9.2b)

parts:
  Arduino1_Slave#2 = Arduino Mini (Rev5)
  Arduino2_Master = Arduino Mini (Rev5)
  U1 = SUP500F [package=sup500f]
  BAT1 = Battery Holders [package=lipo-1100mAh]
  BAT2 = Battery Holders [package=lipo-1100mAh]
  JP1 = Header 1 [part_number="Modem D9" package=smtso-256-et]
  JP2 = Header 1 [part_number="Modem D8" package=smtso-256-et]
  JP3 = Header 1 [part_number="Modem D7" package=smtso-256-et]
  JP4 = Header 1 [part_number="Modem D6" package=smtso-256-et]
  JP5 = Header 1 [part_number="Modem D5" package=smtso-256-et]
  JP6 = Header 1 [part_number="Modem D4" package=smtso-256-et]
  Modem-D3 = Header 1 [part_number="Modem D3" package=smtso-256-et]
  JP8 = Header 1 [part_number="Modem D10" package=smtso-256-et]

nets:
  N1: Arduino1_Slave#2.D3_PWM, Modem-D3.1
  N2: Arduino1_Slave#2.D4, JP6.1
  N3: Arduino1_Slave#2.D5_PWM, JP5.1
  N4: Arduino1_Slave#2.D6_PWM, JP4.1
  N5: Arduino1_Slave#2.D7, JP3.1
  N6: Arduino1_Slave#2.D8, JP2.1
  N7: Arduino1_Slave#2.D9_PWM, JP1.1
  N8: Arduino1_Slave#2.VCC, BAT1.+
  GND: Arduino1_Slave#2.GND, Arduino2_Master.GND, U1.GND, BAT2.-
  5V: Arduino1_Slave#2.5V, Arduino2_Master.5V
  N9: Arduino1_Slave#2.D10_PWM, JP8.1
  N10: Arduino1_Slave#2.A4, Arduino2_Master.A4
  N11: Arduino1_Slave#2.A5, Arduino2_Master.A5
  N12: Arduino2_Master.D3_PWM, U1.TX-O
  N13: Arduino2_Master.D4, U1.RX-I
  N14: U1.VCC, BAT1.-, BAT2.+

notes:
  IEEE SB UMH Stratospheric Balloon, IEEE SB UMH Stratospheric Balloon - GPS and APRS schematic, 1.0
